# Fritzing sketch tübitak (saved by Fritzing 1.0.2b)
breadboards: 1

parts:
  Mod1 = Raspberry Pi Pico
  433T30D1 = 433T30D
  part = Raspberry Pi Zero  # not connected
  Raspberry_Pi_1 = Raspberry Pi 3 [part_number=RPI-3-V1.2]
  X1 = USB Connectors [package=usb-a-s]
  M1 = RioRand LM2596
  J1 = Power Jack [package=power_jack_pth_lock]
  S1 = Taiway 100-SP-X-T1 SPDT Miniature Toggle Switch [part_number=100-SP-X-T1-0-0-B1-M2 package=THT]
  J2 = female pin header, 2 pins [form="♀ (female)"]

nets:
  GND: Mod1.pin_3, Mod1.pin_8, Mod1.pin_13, Mod1.pin_18, Mod1.pin_23, Mod1.pin_28, Mod1.pin_33, Mod1.pin_38, Mod1.pin_42, 433T30D1.M0, 433T30D1.M1, 433T30D1.GND, Raspberry_Pi_1.GND, X1.GND, M1.Pin_4
  N1: Mod1.pin_5, 433T30D1.TXD
  N2: Mod1.pin_6, 433T30D1.RXD
  N3: Mod1.pin_16, Raspberry_Pi_1.GIPO14
  N4: Mod1.pin_40, 433T30D1.VCC, X1.VBUS, M1.Pin_3
  N5: M1.Pin_1, S1.L2, J2.pin2
  N6: M1.Pin_2, J1.GND, J1.GNDBREAK, J2.pin1
  N7: J1.PWR, S1.COM, S1.L1

notes:
  fan

custom parts:
  Raspberry Pi Pico: Raspberry Pi Pico. Based around the RP2040 microcontroller the Pico is a low cost microcontroller device bringing Raspberry Pi quality, cost, and easy of use to the microcontroller space. Jan 2021, Split part in to two versions: tht (this one) and SMD. This one will drill holes for a .1 in header in pcb to allow plugging in the module as well as providing pads to solder the module to the top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
  433T30D: Long Distance Wireless Transceiver UART LoRa Module
